# Fritzing sketch Stoplicht fritzing V1.1 (saved by Fritzing 0.9.3b)
breadboards: 1

parts:
  LED1 = LED - 5mm [color="Red (633nm)" package="5 mm [THT]"]
  R1 = Resistor [tolerance=±5% resistance=220 package=THT]  # not connected
  LED2 = LED - 5mm [color="Red (633nm)" package="5 mm [THT]"]
  LED3 = LED - 5mm [color="Red (633nm)" package="5 mm [THT]"]
  LED4 = LED - 5mm [color="Red (633nm)" package="5 mm [THT]"]  # not connected
  R2 = Resistor [tolerance=±5% resistance=220 package=THT]
  R3 = Resistor [tolerance=±5% resistance=220 package=THT]
  R4 = Resistor [tolerance=±5% resistance=220 package=THT]
  Onderdeel1 = Arduino BT
  LED5 = LED - 5mm [color="Red (633nm)" package="5 mm [THT]"]
  LED6 = LED - 5mm [color="Red (633nm)" package="5 mm [THT]"]
  LED7 = LED - 5mm [color="Red (633nm)" package="5 mm [THT]"]
  LED8 = LED - 5mm [color="Red (633nm)" package="5 mm [THT]"]
  R5 = Resistor [tolerance=±5% resistance=220 package=THT]
  R6 = Resistor [tolerance=±5% resistance=220 package=THT]
  R7 = Resistor [tolerance=±5% resistance=220 package=THT]
  R8 = Resistor [tolerance=±5% resistance=220 package=THT]

nets:
  N1: LED1.anode, Onderdeel1.TX/D1
  N2: LED2.cathode, R2.Pin_1
  N3: LED2.anode, Onderdeel1.D2
  N4: LED3.cathode, R3.Pin_1
  N5: LED3.anode, Onderdeel1.PWM_D3
  N6: R2.Pin_0, R3.Pin_0, R4.Pin_0, Onderdeel1.GND, R5.Pin_1, R6.Pin_1, R7.Pin_1, R8.Pin_1
  N7: Onderdeel1.D8, LED8.cathode
  N8: Onderdeel1.PWM_D9, LED7.cathode
  N9: Onderdeel1.SS/PWM_D10, LED6.cathode
  N10: Onderdeel1.MOSI/PWM_D11, LED5.cathode
  N11: LED5.anode, R5.Pin_0
  N12: LED6.anode, R6.Pin_0
  N13: LED7.anode, R7.Pin_0
  N14: LED8.anode, R8.Pin_0
